// Logisim project microprocessor.circ as structural Verilog: 6 circuits, main circuit CPU
module CPU (
);

  wire Clk, Decode, Execute, Fetch, I_Type, J_Type, P_Type, R_Type;
  wire [2:0] ALU_SEL;
  wire [7:0] Accumulator_q, undriven, Value_Given;
  wire [12:0] inst;

  Register Accumulator (.D(undriven), .Q(Accumulator_q));  // open: en, clk, clr
  Clock u_Clk (.out(Clk));
  Control_Unit Control_Unit (
    .I_Type(I_Type), .R_Type(R_Type), .P_Type(P_Type), .J_Type(J_Type), .Fetch(Fetch), .Decode(Decode),
    .Execute(Execute), .Instruction(inst), .Clk(Clk), .ALU_SEL(ALU_SEL), .Value_Given(Value_Given));
endmodule

// ALU
module AritmaticLogicUnit (
  input  [7:0] Input1,
  input  [7:0] Input2,
  input  [2:0] ALU_SEL,
  output Z,
  output N,
  output C,
  output O,
  output [7:0] Output
);

  wire C_Add, C_Sub, N_Add, N_And, N_Or, N_Sub, O_Add, O_Sub, Z_Add, Z_And, Z_Or, Z_Sub;
  wire [7:0] add, \and , negator_1_out, \or , shiftL, shiftR, sub;

  Negator negator_1 (.in(Input2), .out(negator_1_out));
  Adder adder_1 (.input1(Input1), .input2(Input2), .Output(add), .Carry(C_Add), .Overflow(O_Add));
  Adder adder_2 (.input1(Input1), .input2(negator_1_out), .Output(sub), .Carry(C_Sub), .Overflow(O_Sub));
  assign \and  = Input1 & Input2;  // AND_Gate and, 8 bits wide
  assign \or  = Input1 | Input2;  // OR_Gate or, 8 bits wide
  Shifter shifter_1 (.in(Input1), .\dist (3'b001), .out(shiftL));
  Shifter #(.shift("lr")) shifter_2 (.in(Input1), .\dist (3'b001), .out(shiftR));
  Flag_Control flag_control_1 (.\input (sub), .Negative(N_Sub), .Zero(Z_Sub));
  Flag_Control flag_control_2 (.\input (\and ), .Negative(N_And), .Zero(Z_And));
  Flag_Control flag_control_3 (.\input (\or ), .Negative(N_Or), .Zero(Z_Or));
  Flag_Control flag_control_4 (.\input (add), .Negative(N_Add), .Zero(Z_Add));
  Multiplexer #(.enable("false")) multiplexer_1 (.in0(C_Add), .in1(C_Sub), .out(C), .sel(ALU_SEL[0]));
  Multiplexer #(.enable("false")) multiplexer_2 (.in0(O_Add), .in1(O_Sub), .out(O), .sel(ALU_SEL[0]));
  Multiplexer #(.select(3), .width(8), .enable("false")) multiplexer_3 (
    .in0(add), .in1(sub), .in2(\and ), .in3(\or ), .in4(Input1), .in5(shiftL), .in6(shiftR), .in7({8{1'b0}}),
    .out(Output), .sel(ALU_SEL));

  // Other names for the same wires on the sheet: ALU_SEL_t[2:0] = ALU_SEL; is_sub = ALU_SEL[0]; mov[7:0] = Input1
endmodule

module Accumulator (
  input  [7:0] Input,
  input  Clock,
  input  Exec,
  input  AscSet0,
  output [7:0] \output 
);

  Pull_Resistor pull_resistor_1 (.node(AscSet0));
  D_Flip_Flop d_ff_1 (.clk(Clock), .D(Input[7]), .Q(\output [7]), .en(Exec), .reset(AscSet0));  // open: Qn, preset
  D_Flip_Flop d_ff_2 (.clk(Clock), .D(Input[6]), .Q(\output [6]), .en(Exec), .reset(AscSet0));  // open: Qn, preset
  D_Flip_Flop d_ff_3 (.clk(Clock), .D(Input[5]), .Q(\output [5]), .en(Exec), .reset(AscSet0));  // open: Qn, preset
  D_Flip_Flop d_ff_4 (.clk(Clock), .D(Input[4]), .Q(\output [4]), .en(Exec), .reset(AscSet0));  // open: Qn, preset
  D_Flip_Flop d_ff_5 (.clk(Clock), .D(Input[3]), .Q(\output [3]), .en(Exec), .reset(AscSet0));  // open: Qn, preset
  D_Flip_Flop d_ff_6 (.clk(Clock), .D(Input[2]), .Q(\output [2]), .en(Exec), .reset(AscSet0));  // open: Qn, preset
  D_Flip_Flop d_ff_7 (.clk(Clock), .D(Input[1]), .Q(\output [1]), .en(Exec), .reset(AscSet0));  // open: Qn, preset
  D_Flip_Flop d_ff_8 (.clk(Clock), .D(Input[0]), .Q(\output [0]), .en(Exec), .reset(AscSet0));  // open: Qn, preset

  // Other names for the same wires on the sheet: in0 = Input[0]; in1 = Input[1]; in2 = Input[2]; in3 = Input[3];
  //   in4 = Input[4]; in5 = Input[5]; in6 = Input[6]; in7 = Input[7]; out0 = \output [0]; out1 = \output [1];
  //   out2 = \output [2]; out3 = \output [3]; out4 = \output [4]; out5 = \output [5]; out6 = \output [6];
  //   out7 = \output [7]
endmodule

module Control_Unit (
  input  [12:0] Instruction,
  input  Clk,
  output I_Type,
  output R_Type,
  output P_Type,
  output J_Type,
  output Fetch,
  output Decode,
  output Execute,
  output [7:0] Value_Given,
  output [2:0] ALU_SEL
);

  wire Execute_out, not_1_out, not_2_out, not_3_out, not_4_out, not_5_out, not_6_out, not_7_out, not_8_out,
       not_9_out;
  wire [0:0] or_1_out;
  wire [2:0] register_1_q;

  Decoder #(.select(2), .enable("false")) decoder_1 (
    .out0(I_Type), .out1(R_Type), .out2(P_Type), .out3(J_Type), .sel(Instruction[12:11]));
  Register #(.width(3)) register_1 (
    .D({Fetch, Decode, or_1_out[0]}), .en(1'b1), .Q(register_1_q), .clk(Clk));  // open: clr
  not not_1 (not_1_out, register_1_q[0]);
  not not_2 (not_2_out, register_1_q[1]);
  not not_3 (not_3_out, register_1_q[2]);
  not not_4 (not_4_out, register_1_q[0]);
  and u_Execute (Execute_out, not_1_out, not_2_out, not_3_out);
  or or_1 (or_1_out[0], Execute_out, Execute);
  not not_5 (not_5_out, register_1_q[2]);
  and Execute_2 (Execute, not_4_out, register_1_q[1], not_5_out);
  not not_6 (not_6_out, register_1_q[0]);
  not not_7 (not_7_out, register_1_q[1]);
  and u_Decode (Decode, not_6_out, not_7_out, register_1_q[2]);
  not not_8 (not_8_out, register_1_q[1]);
  not not_9 (not_9_out, register_1_q[2]);
  and u_Fetch (Fetch, register_1_q[0], not_8_out, not_9_out);

  assign ALU_SEL = Instruction[10:8];
  assign Value_Given = Instruction[7:0];

  // Notes on the sheet:
  //   Fetch
  //   Decode
  //   Execute
endmodule

module Adder (
  input  [7:0] input1,
  input  [7:0] input2,
  output [7:0] Output,
  output Carry,
  output Overflow
);

  wire adder_1_cout, adder_2_cout, adder_3_cout, adder_4_cout, adder_5_cout, adder_6_cout, adder_7_cout;

  Adder_part #(.width(1)) adder_1 (.a(input1[0]), .b(input2[0]), .out(Output[0]), .cin(1'b0), .cout(adder_1_cout));
  Adder_part #(.width(1)) adder_2 (
    .a(input1[1]), .b(input2[1]), .out(Output[1]), .cin(adder_1_cout), .cout(adder_2_cout));
  Adder_part #(.width(1)) adder_3 (
    .a(input1[2]), .b(input2[2]), .out(Output[2]), .cin(adder_2_cout), .cout(adder_3_cout));
  Adder_part #(.width(1)) adder_4 (
    .a(input1[3]), .b(input2[3]), .out(Output[3]), .cin(adder_3_cout), .cout(adder_4_cout));
  Adder_part #(.width(1)) adder_5 (
    .a(input1[4]), .b(input2[4]), .out(Output[4]), .cin(adder_4_cout), .cout(adder_5_cout));
  Adder_part #(.width(1)) adder_6 (
    .a(input1[5]), .b(input2[5]), .out(Output[5]), .cin(adder_5_cout), .cout(adder_6_cout));
  Adder_part #(.width(1)) adder_7 (
    .a(input1[6]), .b(input2[6]), .out(Output[6]), .cin(adder_6_cout), .cout(adder_7_cout));
  Adder_part #(.width(1)) adder_8 (.a(input1[7]), .b(input2[7]), .out(Output[7]), .cin(adder_7_cout), .cout(Carry));
  xor xor_1 (Overflow, Carry, adder_7_cout);
endmodule

module Flag_Control (
  input  [7:0] \input ,
  output Negative,
  output Zero
);

  wire or_1_out;

  or or_1 (or_1_out, \input [0], \input [1], \input [2], \input [3], \input [4], \input [5], \input [6], \input [7]);
  not not_1 (Zero, or_1_out);

  assign Negative = \input [7];
endmodule
